# Fritzing sketch barled (saved by Fritzing 0.9.3b)

parts:
  D1 = LED_BARGRAPH_10 [package=led_bargaph_10]
  Componente1 = Arduino Uno (Rev3)

nets:
  N1: D1.A_A, Componente1.D10_PWM/SS
  N2: D1.B_A, Componente1.D9_PWM
  N3: D1.C_A, Componente1.D8
  N4: D1.D_A, Componente1.D7
  N5: D1.E_A, Componente1.D6_PWM
  N6: D1.F_A, Componente1.D5_PWM
  N7: D1.G_A, Componente1.D4
  N8: D1.H_A, Componente1.D3_PWM
  N9: D1.I_A, Componente1.D2
  N10: D1.J_A, Componente1.D1/TX
